# Fritzing sketch rx file (saved by Fritzing 0.9.0b)
breadboards: 1

parts:
  HT12E1 = HT12E [chip_label=HT12E package="DIP (Dual Inline) [THT]"]
  U1 = RF-LINK_RX [package=rf-link_rx]
  IC1 = L293D [package=THT]
  M1 = DC Motor
  M2 = DC Motor
  R1 = Resistor [tolerance=±5% resistance=1M package=THT]

nets:
  N1: HT12E1.A0, HT12E1.A1, HT12E1.A2, HT12E1.A3, HT12E1.A4, HT12E1.A5, HT12E1.A6, HT12E1.A7, HT12E1.VSS, U1.DATA, U1.ANT, IC1.0V
  N2: HT12E1.AD8, IC1.In_4
  N3: HT12E1.AD9, IC1.In_3
  N4: HT12E1.AD10, IC1.In_1
  N5: HT12E1.AD11, IC1.In_2
  N6: HT12E1.OSC2, HT12E1.OSC1, R1.Pin_0, R1.Pin_1
  N7: HT12E1.VDD, IC1.Enable_2, IC1.+V
  N8: IC1.Enable_1, IC1.+Vmotor
  N9: IC1.Out_1_(_Controlled_by_Enable_1_), M2.pin_2
  N10: IC1.Out_2_(_Controlled_by_Enable_1_), M2.pin_1
  N11: IC1.Out_3_(_Controlled_by_Enable_2_), M1.pin_2
  N12: IC1.Out_4_(_Controlled_by_Enable_2_), M1.pin_1

custom parts:
  HT12E: Holtek HT12E 12-bit transmitter encoder. This IC takes a 12-bit input (8 address bits and 4 data bits), encodes and transmits it via a wire, RF transmitter, or IR signal. All input pins may be left open (logical 1) or connected to ground (logical 0). Transmission begins when the TE (Transmission Enable) pin is grounded, and continues as long as TE remains grounded.
