# Fritzing sketch tx file (saved by Fritzing 0.9.0b)
breadboards: 1

parts:
  Part1 = Arduino Uno (Rev3)
  U1 = RF-LINK_TX [package=rf-link_tx]
  HT12E1 = HT12E [chip_label=HT12E package="DIP (Dual Inline) [THT]"]
  R1 = Resistor [tolerance=±5% resistance=1M package=THT]

nets:
  N1: Part1.D3_PWM, HT12E1.AD11
  N2: Part1.D4, HT12E1.AD10
  N3: Part1.D6_PWM, HT12E1.AD9
  N4: Part1.D7, HT12E1.AD8
  5V: Part1.5V, U1.DATA, HT12E1.VDD
  GND: Part1.GND, U1.ANT, HT12E1.A0, HT12E1.A1, HT12E1.A2, HT12E1.A3, HT12E1.A4, HT12E1.A5, HT12E1.A6, HT12E1.A7, HT12E1.VSS, HT12E1.TE
  N5: U1.+5V, HT12E1.DOUT
  N6: HT12E1.OSC2, HT12E1.OSC1, R1.Pin_0, R1.Pin_1

custom parts:
  HT12E: Holtek HT12E 12-bit transmitter encoder. This IC takes a 12-bit input (8 address bits and 4 data bits), encodes and transmits it via a wire, RF transmitter, or IR signal. All input pins may be left open (logical 1) or connected to ground (logical 0). Transmission begins when the TE (Transmission Enable) pin is grounded, and continues as long as TE remains grounded.
